# Fritzing sketch circuit (saved by Fritzing 0.9.3b)

parts:
  Part1 = RFID-RC522-v2
  U2 = NodeMCU V1.0
  Part2 = LCD1602-I2C

nets:
  N1: Part1.SDA, U2.D4
  N2: Part1.SCK, U2.D5
  N3: Part1.MOSI, U2.D7
  N4: Part1.MISO, U2.D6
  GND: Part1.GND, U2.GND, Part2.GND
  N5: Part1.RST, U2.D3
  3.3V: Part1.3.3V, U2.3V3
  N6: U2.D1, Part2.SCL
  N7: U2.D2, Part2.SDA
  VIN: U2.Vin, Part2.VCC

custom parts:
  RFID-RC522-v2: A simple China made RFID-RC522 Reader; do check the pin labels, as this is a MFRC522 based clone.
  NodeMCU V1.0: ESP8266 based NodeMCU
  LCD1602-I2C: A standard character display, usually with 2x16 characters. Comes in many colors with LCM1602 IIC attached.

// code stored in the sketch: hreadv5.ino
//LCD files
#include <LiquidCrystal_I2C.h>

//nodemcu file
#include <ESP8266WiFi.h>

//Firebase File
#include <FirebaseArduino.h>

//RFID reader Files
#include <SPI.h>
#include <MFRC522.h>

//Firebase Variables
#define FIREBASE_HOST "the-wah.firebaseio.com"
#define FIREBASE_AUTH "q9lchUSmqsCKVzfpT19eRZmbC0UtUZIha5cFhHSO"
#define DB_PATH "Assistants/a45vuSucZIaD6BSx49J7HEJJbu12/Doctors/-L6f2Oi2eHAls0g6JwGl/Tokens/"
#define bookedTokensPath "Assistants/a45vuSucZIaD6BSx49J7HEJJbu12/Doctors/-L6f2Oi2eHAls0g6JwGl/bookedTokens"

//Wifi Variables
#define WIFI_SSID "beyond"
#define WIFI_PASSWORD "royalmen"

//nodemcu pins
#define RST_PIN         0           
#define SS_PIN          2         

//required variables
LiquidCrystal_I2C lcd(0x27,16,2);
int currentToken = -1;
MFRC522 mfrc522(SS_PIN, RST_PIN); 

//userdefined functions

void setup() {
//init SPI, Firebase, LCD and MFRC522                                          
  SPI.begin();
  Firebase.begin(FIREBASE_HOST, FIREBASE_AUTH);
  mfrc522.PCD_Init();
  lcd.init();
  lcd.backlight();

//connecting..
  lcd.clear();
  lcd.setCursor(2,0);
  lcd.print(F("Connecting.."));


//wifi connect
  WiFi.begin(WIFI_SSID, WIFI_PASSWORD);
  while (WiFi.status() != WL_CONNECTED) {
  delay(500);
  }

//Starting Message
  lcd.clear();
  lcd.setCursor(2,0);
  lcd.print(F("Dr. P. Kumar"));
  lcd.setCursor(4,1);
  lcd.print(F("Next : 1"));
}

void loop() {
  
  int tokenNumber;
  char tokenChar[18];
  String tokenString, LCD_line1 = "CURRENT : ", LCD_line2 = "NEXT : ";
  
  MFRC522::MIFARE_Key key;
  for (byte i = 0; i < 6; i++) key.keyByte[i] = 0xFF;

  byte len=18;
  
  MFRC522::StatusCode statuss;

//dectecting new card
  if ( ! mfrc522.PICC_IsNewCardPresent()) {
    return;
  }

  if ( ! mfrc522.PICC_ReadCardSerial()) {
    return;
  }
  mfrc522.PICC_DumpDetailsToSerial(&(mfrc522.uid)); 

  byte bufer[18];

//authenticating
  statuss = mfrc522.PCD_Authenticate(MFRC522::PICC_CMD_MF_AUTH_KEY_A, 1, &key, &(mfrc522.uid));
  if (statuss != MFRC522::STATUS_OK) {
    mfrc522.PICC_HaltA();
    mfrc522.PCD_StopCrypto1();
    return;
  }

//reading card
  statuss = mfrc522.MIFARE_Read(1, bufer, &len);
  if (statuss != MFRC522::STATUS_OK) {
    mfrc522.PICC_HaltA();
    mfrc522.PCD_StopCrypto1();
    return;
  }

//converting buffer to Int--------------------------------------
  for (uint8_t i = 0; i < 16; i++) {
    tokenChar[i] = bufer[i];
  }
  tokenChar[17] = '\0';
  tokenString = tokenChar;
  tokenNumber = tokenString.toInt();

  bool nextTokenIsBooked = false;
  int nextToken = tokenNumber;

//get the bookedTokens Array
      FirebaseObject bookedFirebaseObject = Firebase.get(bookedTokensPath);
      if(Firebase.success()){
        JsonArray& bookedTokens = (bookedFirebaseObject.getJsonVariant()).as<JsonArray>();

// get next Token
          while(!nextTokenIsBooked && nextToken <= 100){
            nextToken++;
            for(auto value : bookedTokens){
              if(value.as<int>() == nextToken){
                nextTokenIsBooked = true;
                break;
              }
            }
          }        
      }
      else{
        mfrc522.PICC_HaltA();
        mfrc522.PCD_StopCrypto1();
        return;
      }
 
//LCD variables UPDATE
  LCD_line1 = LCD_line1 + String(tokenNumber);
  if(nextTokenIsBooked){
  LCD_line2 = LCD_line2 + String(nextToken);
//LCD print
    lcd.clear();
    lcd.setCursor(2,0);
    lcd.print(LCD_line1);
    lcd.setCursor(4,1);
    lcd.print(LCD_line2);   
  }
  else{
  LCD_line2 = "No more Tokens";
//LCD print
    lcd.clear();
    lcd.setCursor(2,0);
    lcd.print(LCD_line1);
    lcd.setCursor(1,1);
    lcd.print(LCD_line2);  
  } 
  
//update to Firebase---------------------------------------------
  String dbPath;
  const String state = "/state";

//updating used
  if(currentToken>0){
    dbPath = DB_PATH + String(currentToken) + state;
    Firebase.setString(dbPath, "used");
    if (Firebase.failed()) {  
        mfrc522.PICC_HaltA();
        mfrc522.PCD_StopCrypto1();
        return;
    }  
  }

//updating current
  dbPath = DB_PATH + String(tokenNumber) + state;  
  Firebase.setString(dbPath, "current");
  if (Firebase.failed()) {  
      mfrc522.PICC_HaltA();
      mfrc522.PCD_StopCrypto1();
      return;
  }
  currentToken = tokenNumber;
  
//log upload to firebase------------------------------------------
//  Firebase.pushInt("logs", tokenNumber);
//  if (Firebase.failed()) {   
//      mfrc522.PICC_HaltA();
//      mfrc522.PCD_StopCrypto1();
//      return;
//  }

  delay(1000); 
  mfrc522.PICC_HaltA();
  mfrc522.PCD_StopCrypto1();
}
